# Fritzing sketch BrewNode (saved by Fritzing 0.9.2b)
breadboards: 1

parts:
  Part1 = Arduino Nano (Rev3.0)
  R1 = Resistor [tolerance=±5% resistance=220 package=THT]
  T1 = TMP36 Temperature Sensor [package="TO92 [THT]"]
  NRF24L1 = NRF24L01

nets:
  GND: Part1.GND, T1.GND, NRF24L1.GND
  N1: Part1.D2, NRF24L1.IRQ
  N2: Part1.D4, R1.Pin_0, T1.Vout
  N3: Part1.D9, NRF24L1.CE
  N4: Part1.D10, NRF24L1.CSN
  N5: Part1.D11/MOSI, NRF24L1.MOSI
  N6: Part1.D12/MISO, NRF24L1.MISO
  3V3: Part1.3V3, R1.Pin_1, T1.+Vs, NRF24L1.VCC
  N7: Part1.D13/SCK, NRF24L1.SCK

custom parts:
  NRF24L01: NRF24L01 module
